# Fritzing sketch mineDetector (saved by Fritzing 0.9.3b)
breadboards: 1

parts:
  Raspberry_Pi_1 = Raspberry Pi 3 [part_number=RPI-3-V1.2]
  J1 = Piezo Speaker
  R1 = Resistor [tolerance=±5% resistance=220 package=THT]
  LED1 = LED - 5mm [color="Red (633nm)" package="5 mm [THT]"]
  LED2 = LED - 5mm [color="Yellow (595nm)" package="5 mm [THT]"]
  R2 = Resistor [tolerance=±5% resistance=220 package=THT]
  LED3 = LED - 5mm [color="Green (555nm)" package="5 mm [THT]"]
  LED4 = LED - 5mm [color="Blue (470nm)" package="5 mm [THT]"]
  R3 = Resistor [tolerance=±5% resistance=220 package=THT]
  R4 = Resistor [tolerance=±5% resistance=220 package=THT]

nets:
  N1: Raspberry_Pi_1.GPIO4, J1.pin2
  N2: Raspberry_Pi_1.GPIO17, LED4.anode
  N3: Raspberry_Pi_1.GPIO27, LED3.anode
  N4: Raspberry_Pi_1.GPIO22, LED2.anode
  N5: Raspberry_Pi_1.GPIO16, LED1.anode
  N6: Raspberry_Pi_1.GND, J1.pin1, R1.Pin_1, R2.Pin_1, R3.Pin_1, R4.Pin_1
  N7: R1.Pin_0, LED4.cathode
  N8: LED1.cathode, R4.Pin_0
  N9: LED2.cathode, R3.Pin_0
  N10: R2.Pin_0, LED3.cathode
